// Logisim project practica2Combinatorios.circ as structural Verilog
module main (
  input  in_1,
  input  in_2,
  output out_3
);

  wire and_1_out, not_1_out;

  not not_1 (not_1_out, in_1);
  and and_1 (and_1_out, in_1, in_2);
  or or_1 (out_3, not_1_out, and_1_out);
endmodule

module cuatroA (
  input  in_1,
  input  in_2,
  input  in_3,
  output out_4
);

  wire nor_1_out, not_1_out, not_2_out, not_3_out, not_4_out;

  not not_1 (not_1_out, in_1);
  not not_2 (not_2_out, in_2);
  not not_3 (not_3_out, in_3);
  nor nor_1 (nor_1_out, not_1_out, not_2_out);
  not not_4 (not_4_out, nor_1_out);
  nor nor_2 (out_4, not_4_out, not_3_out);
endmodule

module cuatroB (
  input  in_1,
  input  in_2,
  output out_3
);

  wire not_1_out, not_2_out;

  not not_1 (not_1_out, in_1);
  and and_1 (out_3, not_1_out, not_2_out);
  not not_2 (not_2_out, in_2);
endmodule

module cincoA (
  input  A,
  input  B,
  input  C,
  output out_4
);

  wire and_1_out, and_2_out, not_1_out;

  not not_1 (not_1_out, B);
  and and_1 (and_1_out, A, not_1_out);
  and and_2 (and_2_out, B, C);
  or or_1 (out_4, and_1_out, and_2_out);
endmodule

module cincoB (
  input  D,
  input  E,
  input  F,
  output out_4
);

  wire and_1_out, and_2_out, not_1_out, not_2_out, not_3_out, or_1_out, or_2_out;

  and and_1 (and_1_out, not_1_out, or_1_out);
  or or_1 (or_1_out, not_2_out, F);
  not not_1 (not_1_out, D);
  not not_2 (not_2_out, E);
  not not_3 (not_3_out, F);
  or or_2 (or_2_out, E, not_3_out);
  or or_3 (out_4, and_1_out, and_2_out);
  and and_2 (and_2_out, D, or_2_out);
endmodule

module seisInversorKBits (
  input  C,
  input  e2,
  input  e1,
  input  e0,
  output s2,
  output s1,
  output s0
);

  xor xor_1 (s2, C, e2);
  xor xor_2 (s1, C, e1);
  xor xor_3 (s0, C, e0);
endmodule

module suma1bitcompleta (
  input  A,
  input  B,
  input  Cin,
  output Res,
  output Cflag
);

  wire suma1bitsimple_1_cflag, suma1bitsimple_1_res, suma1bitsimple_2_cflag;

  suma1bitsimple suma1bitsimple_1 (.A(A), .B(B), .Res(suma1bitsimple_1_res), .Cflag(suma1bitsimple_1_cflag));
  suma1bitsimple suma1bitsimple_2 (.A(suma1bitsimple_1_res), .B(Cin), .Res(Res), .Cflag(suma1bitsimple_2_cflag));
  or or_1 (Cflag, suma1bitsimple_2_cflag, suma1bitsimple_1_cflag);
endmodule

module suma1bitsimple (
  input  A,
  input  B,
  output Res,
  output Cflag
);

  xor xor_1 (Res, A, B);
  and and_1 (Cflag, B, A);
endmodule

module sieteInversoAditivoC2 (
  input  e0,
  input  e1,
  input  e2,
  input  e3,
  output s0,
  output s1,
  output s2,
  output s3
);

  wire not_1_out, not_2_out, not_3_out, not_4_out, not_5_out, or_1_out, suma1bitsimple_1_cflag,
       suma1bitsimple_2_cflag, suma1bitsimple_3_cflag;

  not not_1 (not_1_out, e0);
  not not_2 (not_2_out, e1);
  not not_3 (not_3_out, e2);
  not not_4 (not_4_out, e3);
  not not_5 (not_5_out, e3);
  or or_1 (or_1_out, e3, not_5_out);
  suma1bitsimple suma1bitsimple_1 (.A(not_4_out), .B(or_1_out), .Res(s3), .Cflag(suma1bitsimple_1_cflag));
  suma1bitsimple suma1bitsimple_2 (.A(not_3_out), .B(suma1bitsimple_1_cflag), .Res(s2), .Cflag(suma1bitsimple_2_cflag));
  suma1bitsimple suma1bitsimple_3 (.A(not_2_out), .B(suma1bitsimple_2_cflag), .Res(s1), .Cflag(suma1bitsimple_3_cflag));
  suma1bitsimple suma1bitsimple_4 (.A(not_1_out), .B(suma1bitsimple_3_cflag), .Res(s0));  // open: Cflag

  // Notes on the sheet:
  //   Es un truco por si no podes usar el 1 constante
endmodule

module sieteInversoAditivoC2B (
  input  e0,
  input  e1,
  input  e2,
  input  e3,
  output flag,
  output s0,
  output s1,
  output s2,
  output s3
);

  wire and_1_out, nand_1_out, not_1_out, not_2_out, not_3_out, not_4_out, not_5_out, not_6_out, or_1_out,
       suma1bitsimple_1_cflag, suma1bitsimple_2_cflag, suma1bitsimple_3_cflag;

  not not_1 (not_1_out, e0);
  not not_2 (not_2_out, e1);
  not not_3 (not_3_out, e2);
  not not_4 (not_4_out, e3);
  not not_5 (not_5_out, e3);
  or or_1 (or_1_out, e3, not_5_out);
  suma1bitsimple suma1bitsimple_1 (.A(not_4_out), .B(or_1_out), .Res(s3), .Cflag(suma1bitsimple_1_cflag));
  suma1bitsimple suma1bitsimple_2 (.A(not_3_out), .B(suma1bitsimple_1_cflag), .Res(s2), .Cflag(suma1bitsimple_2_cflag));
  suma1bitsimple suma1bitsimple_3 (.A(not_2_out), .B(suma1bitsimple_2_cflag), .Res(s1), .Cflag(suma1bitsimple_3_cflag));
  suma1bitsimple suma1bitsimple_4 (.A(not_1_out), .B(suma1bitsimple_3_cflag), .Res(s0));  // open: Cflag
  and and_1 (and_1_out, s0, not_6_out);
  not not_6 (not_6_out, s1);
  and and_2 (flag, and_1_out, nand_1_out);
  nand nand_1 (nand_1_out, s2, s3);

  // Notes on the sheet:
  //   Es un truco por si no podes usar el 1 constante
  //   Con indicador
endmodule

module ochoDemultiplexor (
  input  c0,
  input  c1,
  input  e0,
  output s0,
  output s1,
  output s2,
  output s3
);

  wire and_1_out, and_2_out, and_3_out, and_4_out, not_1_out, not_2_out, not_3_out, not_4_out;

  not not_1 (not_1_out, c0);
  and and_1 (and_1_out, not_1_out, not_2_out);
  not not_2 (not_2_out, c1);
  not not_3 (not_3_out, c1);
  and and_2 (and_2_out, c0, not_3_out);
  not not_4 (not_4_out, c0);
  and and_3 (and_3_out, not_4_out, c1);
  and and_4 (and_4_out, c0, c1);
  and and_5 (s0, and_1_out, e0);
  and and_6 (s1, and_2_out, e0);
  and and_7 (s2, and_3_out, e0);
  and and_8 (s3, and_4_out, e0);
endmodule

module nueveCodificadorA (
  input  e3,
  input  e2,
  input  e1,
  input  e0,
  output s1,
  output s0
);

  wire and_1_out, and_2_out, not_1_out, not_2_out, not_3_out, not_4_out, xor_1_out, xor_2_out;

  not not_1 (not_1_out, e1);
  not not_2 (not_2_out, e0);
  not not_3 (not_3_out, e2);
  not not_4 (not_4_out, e0);
  xor xor_1 (xor_1_out, e3, e2);
  and and_1 (and_1_out, not_1_out, not_2_out);
  xor xor_2 (xor_2_out, e3, e1);
  and and_2 (and_2_out, not_3_out, not_4_out);
  and and_3 (s1, xor_1_out, and_1_out);
  and and_4 (s0, xor_2_out, and_2_out);

  // Notes on the sheet:
  //   La salida s1 s0 corresponde al num en binario del indice del e
endmodule

module diezDecodificador (
  input  e1,
  input  e0,
  output s3,
  output s2,
  output s1,
  output s0
);

  wire not_1_out, not_2_out, not_3_out, not_4_out;

  and and_1 (s3, e1, e0);
  and and_2 (s2, e1, not_1_out);
  not not_1 (not_1_out, e0);
  not not_2 (not_2_out, e1);
  and and_3 (s1, not_2_out, e0);
  not not_3 (not_3_out, e1);
  and and_4 (s0, not_3_out, not_4_out);
  not not_4 (not_4_out, e0);
endmodule

module diezDemultiplexor (
  input  in_1,
  input  in_2,
  output out_3,
  output out_4,
  output out_5,
  output out_6
);

  diezDecodificador diezdecodificador_1 (.e1(in_1), .e0(in_2), .s3(out_3), .s2(out_4), .s1(out_5), .s0(out_6));
endmodule
